// Logisim project S1-T1.circ as structural Verilog: 9 circuits, main circuit main
module main (
  input  [15:0] in_1,
  input  [15:0] in_2,
  input  [15:0] in_3,
  input  [15:0] in_4,
  input  [15:0] in_5,
  input  [15:0] in_6,
  input  [15:0] in_7,
  input  [15:0] in_8,
  input  [15:0] in_9,
  input  [15:0] in_10,
  input  [15:0] in_11,
  output [15:0] out_12,
  output [15:0] out_13,
  output [15:0] out_14,
  output [15:0] out_15
);

  wire comparator_1_eq, comparator_2_eq, comparator_3_eq, comparator_4_eq,
       lagrangeinterpolationfindvalue_1_out_11, lagrangeinterpolationfindvalue_2_out_11;
  wire [15:0] encrypter_parity_generator_1_encrypted_y1, encrypter_parity_generator_1_encrypted_y2,
       encrypter_parity_generator_1_encrypted_y3, encrypter_parity_generator_1_encrypted_y4,
       encrypter_parity_generator_1_y5, encrypter_parity_generator_1_y6,
       lagrangeinterpolationfindvalue_1_out_10, lagrangeinterpolationfindvalue_2_out_10, multiplexer_1_out,
       multiplexer_2_out, negator_1_out, negator_2_out;

  Encrypter_Parity_generator encrypter_parity_generator_1 (
    .y1(in_1), .y2(in_5), .y3(in_8), .y4(in_10), .public_key(in_11),
    .Encrypted_y1(encrypter_parity_generator_1_encrypted_y1),
    .Encrypted_y2(encrypter_parity_generator_1_encrypted_y2),
    .Encrypted_y3(encrypter_parity_generator_1_encrypted_y3),
    .Encrypted_y4(encrypter_parity_generator_1_encrypted_y4), .y5(encrypter_parity_generator_1_y5),
    .y6(encrypter_parity_generator_1_y6));
  LagrangeInterpolationFindValue lagrangeinterpolationfindvalue_1 (
    .in_1(in_2), .in_2(in_3), .in_3(in_4), .in_4(in_6), .in_5(in_7),
    .in_6(encrypter_parity_generator_1_encrypted_y1), .in_7(encrypter_parity_generator_1_encrypted_y3),
    .in_8(encrypter_parity_generator_1_y5), .in_9(encrypter_parity_generator_1_y6),
    .out_10(lagrangeinterpolationfindvalue_1_out_10), .out_11(lagrangeinterpolationfindvalue_1_out_11));
  LagrangeInterpolationFindValue lagrangeinterpolationfindvalue_2 (
    .in_1(in_9), .in_2(in_3), .in_3(in_4), .in_4(in_6), .in_5(in_7),
    .in_6(encrypter_parity_generator_1_encrypted_y1), .in_7(encrypter_parity_generator_1_encrypted_y3),
    .in_8(encrypter_parity_generator_1_y5), .in_9(encrypter_parity_generator_1_y6),
    .out_10(lagrangeinterpolationfindvalue_2_out_10), .out_11(lagrangeinterpolationfindvalue_2_out_11));
  Negator #(.width(16)) negator_1 (.in(lagrangeinterpolationfindvalue_1_out_10), .out(negator_1_out));
  Negator #(.width(16)) negator_2 (.in(lagrangeinterpolationfindvalue_2_out_10), .out(negator_2_out));
  Multiplexer #(.width(16)) multiplexer_1 (
    .in0(lagrangeinterpolationfindvalue_1_out_10), .in1(negator_1_out), .out(multiplexer_1_out),
    .sel(lagrangeinterpolationfindvalue_1_out_11));  // open: en
  Multiplexer #(.width(16)) multiplexer_2 (
    .in0(lagrangeinterpolationfindvalue_2_out_10), .in1(negator_2_out), .out(multiplexer_2_out),
    .sel(lagrangeinterpolationfindvalue_2_out_11));  // open: en
  Decryptor decryptor_1 (
    .in_1(encrypter_parity_generator_1_encrypted_y1), .in_2(multiplexer_1_out),
    .in_3(encrypter_parity_generator_1_encrypted_y3), .in_4(multiplexer_2_out), .in_5(in_11), .out_6(out_12),
    .out_7(out_13), .out_8(out_14), .out_9(out_15));
  Comparator #(.width(16)) comparator_1 (.a(in_1), .b(out_12), .eq(comparator_1_eq));  // open: gt, lt
  Comparator #(.width(16)) comparator_2 (.a(in_8), .b(out_14), .eq(comparator_2_eq));  // open: gt, lt
  Comparator #(.width(16)) comparator_3 (.a(in_10), .b(out_15), .eq(comparator_3_eq));  // open: gt, lt
  LED led_1 (.in(comparator_1_eq));
  Comparator #(.width(16)) comparator_4 (.a(in_5), .b(out_13), .eq(comparator_4_eq));  // open: gt, lt
  LED led_2 (.in(comparator_3_eq));
  LED led_3 (.in(comparator_4_eq));
  LED led_4 (.in(comparator_2_eq));

  // Notes on the sheet:
  //   y1
  //   y2
  //   y3
  //   y4
  //   Key
  //   INPUTS : 4 4bit Values and User Input Key
  //   Encrypted y's
  //   Instructions : Input any 4 bit values and any use any input key  
  //   1,3,5,6
  //   X
  //   X
  //   Let the 2nd and 4th value be lost
  //   4 (Index value to be found)
  //   KEY
  //   OUTPUTS : Input values are regenerated and are checked using comparators
  //   2 (Index value to be found)
  //   Generating values for Lagrange Interpolation
  //   S1-T1
  //   Generating values for Lagrange Interpolation
  //   y2 (recovered)
  //   y4 (recovered)
  //   Vignere Cipher encrypter
  //   Vignere Cipher decrypter
  //   Calculating Extra bits for error correction
  //   Comparator to check and verify
  //   Components Used :
  //   Finding values for Lagrange Polynomials
  //   SubCircuit to handle improper and negative fractions
  //   Decrypter
  //   Value 1 regenerated
  //   y1
  //   Value 4 regenrated
  //   Value 2 regenerated
  //   y2
  //   y3
  //   y4
  //   Value 3 regenerated
endmodule

module ProdOfSubtr (
  input  [15:0] in_1,
  input  [15:0] in_2,
  input  [15:0] in_3,
  input  [15:0] in_4,
  output [15:0] out_5,
  output out_6
);

  wire subtractor_1_bout, subtractor_2_bout, subtractor_3_bout, xor_1_out;
  wire [15:0] multiplexer_1_out, multiplexer_2_out, multiplexer_3_out, multiplier_1_out, subtractor_1_out,
       subtractor_2_out, subtractor_3_out, subtractor_4_out, subtractor_5_out, subtractor_6_out;

  Subtractor #(.width(16)) subtractor_1 (
    .a(in_1), .b(in_2), .out(subtractor_1_out), .bin(1'b0), .bout(subtractor_1_bout));
  Subtractor #(.width(16)) subtractor_2 (
    .a(in_1), .b(in_3), .out(subtractor_2_out), .bin(1'b0), .bout(subtractor_2_bout));
  Subtractor #(.width(16)) subtractor_3 (
    .a(in_1), .b(in_4), .out(subtractor_3_out), .bin(1'b0), .bout(subtractor_3_bout));
  Subtractor #(.width(16)) subtractor_4 (
    .a({16{1'b0}}), .b(subtractor_1_out), .out(subtractor_4_out));  // open: bin, bout
  Multiplexer #(.width(16)) multiplexer_1 (
    .in0(subtractor_1_out), .in1(subtractor_4_out), .out(multiplexer_1_out), .sel(subtractor_1_bout));  // open: en
  Subtractor #(.width(16)) subtractor_5 (
    .a({16{1'b0}}), .b(subtractor_2_out), .out(subtractor_5_out));  // open: bin, bout
  Multiplexer #(.width(16)) multiplexer_2 (
    .in0(subtractor_2_out), .in1(subtractor_5_out), .out(multiplexer_2_out), .sel(subtractor_2_bout));  // open: en
  Subtractor #(.width(16)) subtractor_6 (
    .a({16{1'b0}}), .b(subtractor_3_out), .out(subtractor_6_out));  // open: bin, bout
  Multiplexer #(.width(16)) multiplexer_3 (
    .in0(subtractor_3_out), .in1(subtractor_6_out), .out(multiplexer_3_out), .sel(subtractor_3_bout));  // open: en
  Multiplier #(.width(16)) multiplier_1 (
    .a(multiplexer_1_out), .b(multiplexer_2_out), .out(multiplier_1_out));  // open: cin, cout
  Multiplier #(.width(16)) multiplier_2 (.a(multiplier_1_out), .b(multiplexer_3_out), .out(out_5));  // open: cin, cout
  xor xor_1 (xor_1_out, subtractor_1_bout, subtractor_2_bout);
  xor xor_2 (out_6, subtractor_3_bout, xor_1_out);

  // Notes on the sheet:
  //   x_input
  //   x2
  //   x3
  //   x4
  //   Absolute vaue for the expression
  //   (x_input - x2)(x_input - x3)(x_nput - x4)
  //   0 if positive and 1 if negative
endmodule

module ImproperFractionTerm (
  input  [15:0] in_1,
  input  [15:0] in_2,
  input  [15:0] in_3,
  input  [15:0] in_4,
  input  [15:0] in_5,
  input  [15:0] in_6,
  output [15:0] out_7,
  output [15:0] out_8,
  output out_9
);

  wire prodofsubtr_1_out_6, prodofsubtr_2_out_6, xor_1_out;
  wire [15:0] multiplexer_1_out, negator_1_out, prodofsubtr_1_out_5;

  ProdOfSubtr prodofsubtr_1 (
    .in_1(in_1), .in_2(in_3), .in_3(in_4), .in_4(in_5), .out_5(prodofsubtr_1_out_5),
    .out_6(prodofsubtr_1_out_6));
  Negator #(.width(16)) negator_1 (.in(in_6), .out(negator_1_out));
  ProdOfSubtr prodofsubtr_2 (
    .in_1(in_2), .in_2(in_3), .in_3(in_4), .in_4(in_5), .out_5(out_8), .out_6(prodofsubtr_2_out_6));
  Multiplexer #(.width(16)) multiplexer_1 (
    .in0(in_6), .in1(negator_1_out), .out(multiplexer_1_out), .sel(in_6[15]));  // open: en
  Multiplier #(.width(16)) multiplier_1 (
    .a(prodofsubtr_1_out_5), .b(multiplexer_1_out), .out(out_7));  // open: cin, cout
  xor xor_1 (xor_1_out, prodofsubtr_1_out_6, prodofsubtr_2_out_6);
  xor xor_2 (out_9, xor_1_out, in_6[15]);

  // Notes on the sheet:
  //   x_input
  //   x1
  //   x2
  //   x3
  //   x4
  //   y1
  //   Write y1 in 2s complement if negative
  //   Absolute Value of Numerator
  //   Absolute Value of Denominator
  //   1 for -ve and 0 for +ve
endmodule

module LCMofDenominator_NumeratorUpdation (
  input  [15:0] in_1,
  input  [15:0] in_2,
  input  [15:0] in_3,
  input  [15:0] in_4,
  input  [15:0] in_5,
  input  [15:0] in_6,
  input  [15:0] in_7,
  input  [15:0] in_8,
  input  [15:0] in_9,
  output [15:0] out_10,
  output [15:0] out_11,
  output Num1_Sign,
  output [15:0] out_13,
  output Num2_Sign,
  output [15:0] out_15,
  output Num3_Sign,
  output [15:0] out_17,
  output Num4_Sign
);

  wire [15:0] divider_1_out, divider_2_out, divider_3_out, divider_4_out, improperfractionterm_1_out_7,
       improperfractionterm_1_out_8, improperfractionterm_2_out_7, improperfractionterm_2_out_8,
       improperfractionterm_3_out_7, improperfractionterm_3_out_8, improperfractionterm_4_out_7,
       improperfractionterm_4_out_8, multiplier_1_out, multiplier_2_out;

  ImproperFractionTerm improperfractionterm_1 (
    .in_1(in_1), .in_2(in_2), .in_3(in_3), .in_4(in_4), .in_5(in_5), .in_6(in_6),
    .out_7(improperfractionterm_1_out_7), .out_8(improperfractionterm_1_out_8), .out_9(Num1_Sign));
  ImproperFractionTerm improperfractionterm_2 (
    .in_1(in_1), .in_2(in_3), .in_3(in_2), .in_4(in_4), .in_5(in_5), .in_6(in_7),
    .out_7(improperfractionterm_2_out_7), .out_8(improperfractionterm_2_out_8), .out_9(Num2_Sign));
  ImproperFractionTerm improperfractionterm_3 (
    .in_1(in_1), .in_2(in_4), .in_3(in_2), .in_4(in_3), .in_5(in_5), .in_6(in_8),
    .out_7(improperfractionterm_3_out_7), .out_8(improperfractionterm_3_out_8), .out_9(Num3_Sign));
  ImproperFractionTerm improperfractionterm_4 (
    .in_1(in_1), .in_2(in_5), .in_3(in_2), .in_4(in_3), .in_5(in_4), .in_6(in_9),
    .out_7(improperfractionterm_4_out_7), .out_8(improperfractionterm_4_out_8), .out_9(Num4_Sign));
  Multiplier #(.width(16)) multiplier_1 (
    .a(improperfractionterm_1_out_8), .b(improperfractionterm_3_out_8), .out(multiplier_1_out));  // open: cin, cout
  Multiplier #(.width(16)) multiplier_2 (
    .a(improperfractionterm_4_out_8), .b(improperfractionterm_2_out_8), .out(multiplier_2_out));  // open: cin, cout
  Multiplier #(.width(16)) multiplier_3 (.a(multiplier_1_out), .b(multiplier_2_out), .out(out_10));  // open: cin, cout
  Divider #(.width(16)) divider_1 (
    .a(out_10), .b(improperfractionterm_1_out_8), .out(divider_1_out));  // open: upper, rem
  Divider #(.width(16)) divider_2 (
    .a(out_10), .b(improperfractionterm_2_out_8), .out(divider_2_out));  // open: upper, rem
  Divider #(.width(16)) divider_3 (
    .a(out_10), .b(improperfractionterm_3_out_8), .out(divider_3_out));  // open: upper, rem
  Divider #(.width(16)) divider_4 (
    .a(out_10), .b(improperfractionterm_4_out_8), .out(divider_4_out));  // open: upper, rem
  Multiplier #(.width(16)) multiplier_4 (
    .a(divider_1_out), .b(improperfractionterm_1_out_7), .out(out_11));  // open: cin, cout
  Multiplier #(.width(16)) multiplier_5 (
    .a(divider_2_out), .b(improperfractionterm_2_out_7), .out(out_13));  // open: cin, cout
  Multiplier #(.width(16)) multiplier_6 (
    .a(divider_3_out), .b(improperfractionterm_3_out_7), .out(out_15));  // open: cin, cout
  Multiplier #(.width(16)) multiplier_7 (
    .a(divider_4_out), .b(improperfractionterm_4_out_7), .out(out_17));  // open: cin, cout

  // Notes on the sheet:
  //   x_input
  //   x1
  //   x2
  //   x3
  //   x4
  //   y1
  //   y2
  //   y3
  //   y4
  //   N1/D1
  //   N2/D2
  //   N3/D3
  //   N4/D4
  //   LCM of Denominators
  //   Numerator2 After Taking LCM
  //   LCM Of Denominators
  //   (NOTE : All Numerators are Absolute Values)
  //   Numerator1 After Taking LCM
  //   Numerator3 After Taking LCM
  //   Numerator4 After Taking LCM
endmodule

module SummationOfAllParts_FractionDivision (
  input  [15:0] in_1,
  input  [15:0] in_2,
  input  [15:0] in_3,
  input  [15:0] in_4,
  input  [15:0] in_5,
  input  [15:0] in_6,
  input  [15:0] in_7,
  input  [15:0] in_8,
  input  [15:0] in_9,
  output [15:0] out_10,
  output Sign_of_Output
);

  wire lcmofdenominator_numeratorupdation_1_num1_sign, lcmofdenominator_numeratorupdation_1_num2_sign,
       lcmofdenominator_numeratorupdation_1_num3_sign, lcmofdenominator_numeratorupdation_1_num4_sign;
  wire [14:0] adder_3_out;
  wire [15:0] adder_1_out, adder_2_out, lcmofdenominator_numeratorupdation_1_out_10,
       lcmofdenominator_numeratorupdation_1_out_11, lcmofdenominator_numeratorupdation_1_out_13,
       lcmofdenominator_numeratorupdation_1_out_15, lcmofdenominator_numeratorupdation_1_out_17,
       multiplexer_1_out, multiplexer_2_out, multiplexer_3_out, multiplexer_4_out, multiplexer_5_out,
       negator_1_out, negator_2_out, negator_3_out, negator_4_out, negator_5_out;

  LCMofDenominator_NumeratorUpdation lcmofdenominator_numeratorupdation_1 (
    .in_1(in_1), .in_2(in_2), .in_3(in_3), .in_4(in_4), .in_5(in_5), .in_6(in_6), .in_7(in_7), .in_8(in_8),
    .in_9(in_9), .out_10(lcmofdenominator_numeratorupdation_1_out_10),
    .out_11(lcmofdenominator_numeratorupdation_1_out_11),
    .Num1_Sign(lcmofdenominator_numeratorupdation_1_num1_sign),
    .out_13(lcmofdenominator_numeratorupdation_1_out_13),
    .Num2_Sign(lcmofdenominator_numeratorupdation_1_num2_sign),
    .out_15(lcmofdenominator_numeratorupdation_1_out_15),
    .Num3_Sign(lcmofdenominator_numeratorupdation_1_num3_sign),
    .out_17(lcmofdenominator_numeratorupdation_1_out_17),
    .Num4_Sign(lcmofdenominator_numeratorupdation_1_num4_sign));
  Negator #(.width(16)) negator_1 (.in(lcmofdenominator_numeratorupdation_1_out_11), .out(negator_1_out));
  Multiplexer #(.width(16)) multiplexer_1 (
    .in0(lcmofdenominator_numeratorupdation_1_out_11), .in1(negator_1_out), .out(multiplexer_1_out),
    .sel(lcmofdenominator_numeratorupdation_1_num1_sign));  // open: en
  Negator #(.width(16)) negator_2 (.in(lcmofdenominator_numeratorupdation_1_out_13), .out(negator_2_out));
  Negator #(.width(16)) negator_3 (.in(lcmofdenominator_numeratorupdation_1_out_15), .out(negator_3_out));
  Negator #(.width(16)) negator_4 (.in(lcmofdenominator_numeratorupdation_1_out_17), .out(negator_4_out));
  Adder #(.width(16)) adder_1 (.a(multiplexer_1_out), .b(multiplexer_2_out), .out(adder_1_out));  // open: cin, cout
  Multiplexer #(.width(16)) multiplexer_2 (
    .in0(lcmofdenominator_numeratorupdation_1_out_13), .in1(negator_2_out), .out(multiplexer_2_out),
    .sel(lcmofdenominator_numeratorupdation_1_num2_sign));  // open: en
  Multiplexer #(.width(16)) multiplexer_3 (
    .in0(lcmofdenominator_numeratorupdation_1_out_15), .in1(negator_3_out), .out(multiplexer_3_out),
    .sel(lcmofdenominator_numeratorupdation_1_num3_sign));  // open: en
  Multiplexer #(.width(16)) multiplexer_4 (
    .in0(lcmofdenominator_numeratorupdation_1_out_17), .in1(negator_4_out), .out(multiplexer_4_out),
    .sel(lcmofdenominator_numeratorupdation_1_num4_sign));  // open: en
  Adder #(.width(16)) adder_2 (.a(multiplexer_3_out), .b(multiplexer_4_out), .out(adder_2_out));  // open: cin, cout
  Adder #(.width(16)) adder_3 (
    .a(adder_1_out), .b(adder_2_out), .out({Sign_of_Output, adder_3_out}));  // open: cin, cout
  Multiplexer #(.width(16)) multiplexer_5 (
    .in0({Sign_of_Output, adder_3_out}), .in1(negator_5_out), .out(multiplexer_5_out), .sel(Sign_of_Output));  // open: en
  Negator #(.width(16)) negator_5 (.in({Sign_of_Output, adder_3_out}), .out(negator_5_out));
  Divider #(.width(16)) divider_1 (
    .a(multiplexer_5_out), .b(lcmofdenominator_numeratorupdation_1_out_10), .out(out_10));  // open: upper, rem

  // Notes on the sheet:
  //   x_input
  //   x1
  //   x2
  //   x3
  //   x4
  //   y1
  //   y2
  //   y3
  //   y4
  //   Final LCM Denominator
  //   Final Numerator
  //   Absolute Value of the Summed Numerator
  //   Sign of the summed Numerator
  //   Absolute Value of Output
endmodule

module LagrangeInterpolationFindValue (
  input  [15:0] in_1,
  input  [15:0] in_2,
  input  [15:0] in_3,
  input  [15:0] in_4,
  input  [15:0] in_5,
  input  [15:0] in_6,
  input  [15:0] in_7,
  input  [15:0] in_8,
  input  [15:0] in_9,
  output [15:0] out_10,
  output out_11
);

  SummationOfAllParts_FractionDivision summationofallparts_fractiondivision_1 (
    .in_1(in_1), .in_2(in_2), .in_3(in_3), .in_4(in_4), .in_5(in_5), .in_6(in_6), .in_7(in_7), .in_8(in_8),
    .in_9(in_9), .out_10(out_10), .Sign_of_Output(out_11));

  // Notes on the sheet:
  //   x_input
  //   x1
  //   x2
  //   x3
  //   x4
  //   y1
  //   y2
  //   y3
  //   y4
  //   Y_output (Absolute Value)
  //   Sign Of the Output
  //   1 for Negative and 0 for Positive
endmodule

module Encrypter_Parity_generator (
  input  [15:0] y1,
  input  [15:0] y2,
  input  [15:0] y3,
  input  [15:0] y4,
  input  [15:0] public_key,
  output [15:0] Encrypted_y1,
  output [15:0] Encrypted_y2,
  output [15:0] Encrypted_y3,
  output [15:0] Encrypted_y4,
  output [15:0] y5,
  output [15:0] y6
);

  wire lagrangeinterpolationfindvalue_1_out_11, lagrangeinterpolationfindvalue_2_out_11;
  wire [15:0] adder_1_out, adder_2_out, adder_3_out, adder_4_out, lagrangeinterpolationfindvalue_1_out_10,
       lagrangeinterpolationfindvalue_2_out_10, negator_1_out, negator_2_out;

  Adder #(.width(16)) adder_1 (.a(y1), .b(public_key), .out(adder_1_out));  // open: cin, cout
  Adder #(.width(16)) adder_2 (.a(y2), .b(public_key), .out(adder_2_out));  // open: cin, cout
  Adder #(.width(16)) adder_3 (.a(y3), .b(public_key), .out(adder_3_out));  // open: cin, cout
  Adder #(.width(16)) adder_4 (.a(y4), .b(public_key), .out(adder_4_out));  // open: cin, cout
  Divider #(.width(16)) divider_1 (.a(adder_1_out), .b(16'h10), .rem(Encrypted_y1));  // open: out, upper
  Divider #(.width(16)) divider_2 (.a(adder_2_out), .b(16'h10), .rem(Encrypted_y2));  // open: out, upper
  Divider #(.width(16)) divider_3 (.a(adder_3_out), .b(16'h10), .rem(Encrypted_y3));  // open: out, upper
  Divider #(.width(16)) divider_4 (.a(adder_4_out), .b(16'h10), .rem(Encrypted_y4));  // open: out, upper
  LagrangeInterpolationFindValue lagrangeinterpolationfindvalue_1 (
    .in_1(16'h5), .in_2(16'h1), .in_3(16'h2), .in_4(16'h3), .in_5(16'h4), .in_6(Encrypted_y1),
    .in_7(Encrypted_y2), .in_8(Encrypted_y3), .in_9(Encrypted_y4),
    .out_10(lagrangeinterpolationfindvalue_1_out_10), .out_11(lagrangeinterpolationfindvalue_1_out_11));
  LagrangeInterpolationFindValue lagrangeinterpolationfindvalue_2 (
    .in_1(16'h6), .in_2(16'h1), .in_3(16'h2), .in_4(16'h3), .in_5(16'h4), .in_6(Encrypted_y1),
    .in_7(Encrypted_y2), .in_8(Encrypted_y3), .in_9(Encrypted_y4),
    .out_10(lagrangeinterpolationfindvalue_2_out_10), .out_11(lagrangeinterpolationfindvalue_2_out_11));
  Negator #(.width(16)) negator_1 (.in(lagrangeinterpolationfindvalue_1_out_10), .out(negator_1_out));
  Negator #(.width(16)) negator_2 (.in(lagrangeinterpolationfindvalue_2_out_10), .out(negator_2_out));
  Multiplexer #(.width(16)) multiplexer_1 (
    .in0(lagrangeinterpolationfindvalue_1_out_10), .in1(negator_1_out), .out(y5),
    .sel(lagrangeinterpolationfindvalue_1_out_11));  // open: en
  Multiplexer #(.width(16)) multiplexer_2 (
    .in0(lagrangeinterpolationfindvalue_2_out_10), .in1(negator_2_out), .out(y6),
    .sel(lagrangeinterpolationfindvalue_2_out_11));  // open: en
endmodule

module BUFFER (
  input  [15:0] y1,
  input  [15:0] y2,
  input  [15:0] y3,
  input  [15:0] y4,
  input  [15:0] public_key
);

  wire and_1_out, button_1_out, button_2_out, comparator_1_eq, comparator_2_eq, comparator_3_eq,
       comparator_4_eq;
  wire [15:0] register_1_q, register_2_q, register_3_q, register_4_q;

  Button button_1 (.out(button_1_out));
  Register #(.width(16)) register_1 (.D(y1), .Q(register_1_q), .clk(button_1_out), .clr(button_2_out));  // open: en
  Register #(.width(16)) register_2 (.D(y2), .Q(register_2_q), .clk(button_1_out), .clr(button_2_out));  // open: en
  Register #(.width(16)) register_3 (.D(y3), .Q(register_3_q), .clk(button_1_out), .clr(button_2_out));  // open: en
  Register #(.width(16)) register_4 (.D(y4), .Q(register_4_q), .clk(button_1_out), .clr(button_2_out));  // open: en
  Button button_2 (.out(button_2_out));
  Comparator #(.width(16)) comparator_1 (.a(register_1_q), .eq(comparator_1_eq));  // open: b, gt, lt
  Comparator #(.width(16)) comparator_2 (.a(register_2_q), .eq(comparator_2_eq));  // open: b, gt, lt
  Comparator #(.width(16)) comparator_3 (.a(register_3_q), .eq(comparator_3_eq));  // open: b, gt, lt
  Comparator #(.width(16)) comparator_4 (.a(register_4_q), .eq(comparator_4_eq));  // open: b, gt, lt
  Adder #(.width(16)) adder_1 (.a(y1), .b(public_key));  // open: out, cin, cout
  Adder #(.width(16)) adder_2 (.a(y2), .b(public_key));  // open: out, cin, cout
  Adder #(.width(16)) adder_3 (.a(y3), .b(public_key));  // open: out, cin, cout
  Adder #(.width(16)) adder_4 (.a(y4), .b(public_key));  // open: out, cin, cout
  and and_1 (and_1_out, comparator_1_eq, comparator_2_eq, comparator_3_eq, comparator_4_eq);

  // Notes on the sheet:
  //   set
  //   reset
endmodule

module Decryptor (
  input  [15:0] in_1,
  input  [15:0] in_2,
  input  [15:0] in_3,
  input  [15:0] in_4,
  input  [15:0] in_5,
  output [15:0] out_6,
  output [15:0] out_7,
  output [15:0] out_8,
  output [15:0] out_9
);

  wire [15:0] divider_1_rem, divider_2_rem, divider_3_rem, divider_4_rem, multiplexer_1_out,
       multiplexer_2_out, multiplexer_3_out, multiplexer_4_out, negator_1_out, negator_2_out, negator_3_out,
       negator_4_out, subtractor_1_out, subtractor_2_out, subtractor_3_out, subtractor_4_out,
       subtractor_5_out, subtractor_6_out, subtractor_7_out, subtractor_8_out;

  Subtractor #(.width(16)) subtractor_1 (.a(in_1), .b(in_5), .out(subtractor_1_out));  // open: bin, bout
  Subtractor #(.width(16)) subtractor_2 (.a(in_2), .b(in_5), .out(subtractor_2_out));  // open: bin, bout
  Subtractor #(.width(16)) subtractor_3 (.a(in_3), .b(in_5), .out(subtractor_3_out));  // open: bin, bout
  Subtractor #(.width(16)) subtractor_4 (.a(in_4), .b(in_5), .out(subtractor_4_out));  // open: bin, bout
  Negator #(.width(16)) negator_1 (.in(subtractor_1_out), .out(negator_1_out));
  Negator #(.width(16)) negator_2 (.in(subtractor_2_out), .out(negator_2_out));
  Negator #(.width(16)) negator_3 (.in(subtractor_3_out), .out(negator_3_out));
  Negator #(.width(16)) negator_4 (.in(subtractor_4_out), .out(negator_4_out));
  Multiplexer #(.width(16)) multiplexer_1 (
    .in0(subtractor_1_out), .in1(negator_1_out), .out(multiplexer_1_out), .sel(subtractor_1_out[15]));  // open: en
  Multiplexer #(.width(16)) multiplexer_2 (
    .in0(subtractor_2_out), .in1(negator_2_out), .out(multiplexer_2_out), .sel(subtractor_2_out[15]));  // open: en
  Multiplexer #(.width(16)) multiplexer_3 (
    .in0(subtractor_3_out), .in1(negator_3_out), .out(multiplexer_3_out), .sel(subtractor_3_out[15]));  // open: en
  Multiplexer #(.width(16)) multiplexer_4 (
    .in0(subtractor_4_out), .in1(negator_4_out), .out(multiplexer_4_out), .sel(subtractor_4_out[15]));  // open: en
  Divider #(.width(16)) divider_1 (.a(multiplexer_1_out), .b(16'h10), .rem(divider_1_rem));  // open: out, upper
  Divider #(.width(16)) divider_2 (.a(multiplexer_2_out), .b(16'h10), .rem(divider_2_rem));  // open: out, upper
  Divider #(.width(16)) divider_3 (.a(multiplexer_3_out), .b(16'h10), .rem(divider_3_rem));  // open: out, upper
  Divider #(.width(16)) divider_4 (.a(multiplexer_4_out), .b(16'h10), .rem(divider_4_rem));  // open: out, upper
  Subtractor #(.width(16)) subtractor_5 (.a(16'h10), .b(divider_1_rem), .out(subtractor_5_out));  // open: bin, bout
  Multiplexer #(.width(16)) multiplexer_5 (
    .in0(divider_1_rem), .in1(subtractor_5_out), .out(out_6), .sel(subtractor_1_out[15]));  // open: en
  Subtractor #(.width(16)) subtractor_6 (.a(16'h10), .b(divider_2_rem), .out(subtractor_6_out));  // open: bin, bout
  Multiplexer #(.width(16)) multiplexer_6 (
    .in0(divider_2_rem), .in1(subtractor_6_out), .out(out_7), .sel(subtractor_2_out[15]));  // open: en
  Subtractor #(.width(16)) subtractor_7 (.a(16'h10), .b(divider_3_rem), .out(subtractor_7_out));  // open: bin, bout
  Multiplexer #(.width(16)) multiplexer_7 (
    .in0(divider_3_rem), .in1(subtractor_7_out), .out(out_8), .sel(subtractor_3_out[15]));  // open: en
  Subtractor #(.width(16)) subtractor_8 (.a(16'h10), .b(divider_4_rem), .out(subtractor_8_out));  // open: bin, bout
  Multiplexer #(.width(16)) multiplexer_8 (
    .in0(divider_4_rem), .in1(subtractor_8_out), .out(out_9), .sel(subtractor_4_out[15]));  // open: en

  // Notes on the sheet:
  //   Num1
  //   Num2
  //   Num3
  //   Num4
  //   KEY
endmodule
